# Fritzing sketch board (saved by Fritzing 0.9.3b)
breadboards: 1

parts:
  R1 = Resistor [tolerance=±5% resistance=560 package=THT]
  R2 = Resistor [tolerance=±5% resistance=1k package=THT]
  R3 = Resistor [tolerance=±5% resistance=10k package=THT]
  Componente1 = Arduino Uno (Rev3)
  J1 = Piezo Speaker
  S1 = Pushbutton [package="[THT]"]
  LED1 = LED - 3mm [color="Green (555nm)" package="3 mm [THT]"]

nets:
  N1: R1.Pin_0, Componente1.D13/SCK
  N2: R1.Pin_1, LED1.cathode
  N3: R2.Pin_0, Componente1.D12/MISO
  N4: R2.Pin_1, J1.pin2
  N5: R3.Pin_0, Componente1.D2, S1.Pin_1, S1.Pin_2
  N6: R3.Pin_1, Componente1.GND, J1.pin1, LED1.anode
  N7: Componente1.5V, S1.Pin_3, S1.Pin_4
